# Fritzing sketch AlarmaMailPir (saved by Fritzing 0.9.0b)
breadboards: 1

parts:
  Raspberry_Pi_B_rev1 = Raspberry Pi B rev1
  PIR1 = PIR sensor
  LED1 = smd LED [color="Red (633nm)" package="0805 [SMD]"]
  R1 = Resistor [tolerance=±5% resistance=220 package=THT]

nets:
  3V3: Raspberry_Pi_B_rev1.3V3, Raspberry_Pi_B_rev1.5V, Raspberry_Pi_B_rev1.GPIO_0, Raspberry_Pi_B_rev1.GPIO_24, PIR1.VDD
  GND: Raspberry_Pi_B_rev1.GPIO_1, Raspberry_Pi_B_rev1.GND, Raspberry_Pi_B_rev1.GPIO_15, Raspberry_Pi_B_rev1.GPIO_21, Raspberry_Pi_B_rev1.GPIO_10, Raspberry_Pi_B_rev1.GPIO_7, PIR1.GND, LED1.cathode
  N1: Raspberry_Pi_B_rev1.GPIO_23, Raspberry_Pi_B_rev1.GPIO_22
  N2: Raspberry_Pi_B_rev1.GPIO_14, Raspberry_Pi_B_rev1.GPIO_4
  N3: Raspberry_Pi_B_rev1.GPIO_17, Raspberry_Pi_B_rev1.GPIO_18, PIR1.SIG
  N4: Raspberry_Pi_B_rev1.GPIO_9, Raspberry_Pi_B_rev1.GPIO_25
  N5: Raspberry_Pi_B_rev1.GPIO_11, Raspberry_Pi_B_rev1.GPIO_8
  N6: LED1.anode, R1.Pin_1

notes:
  ALARMA CON SENSOR DE PRESENCIA PIR Y PROGRAMADA EN PYTHON QUE ENVÍA UN MAIL EN CASO DETECTAR INTRUSIÓN.
